# Fritzing sketch DHT22Sensor (saved by Fritzing 1.0.1rc)
breadboards: 1

parts:
  U2 = XBEE-1 [package=xbee-1_lock]
  LED1 = LED - 5mm [color="Red (633nm)" current=0.030 package="5 mm [THT]"]
  S1 = Pushbutton [package="[THT]"]
  R2 = Resistor [tolerance=±5% power=0.25 resistance=330 package=THT]
  R1 = Resistor [tolerance=±5% power=0.25 resistance=10k package=THT]
  U1 = Arduino Pro Micro (Clone)
  U3 = DHT22 Humidity and Temperature Sensor
  C1 = Ceramic Capacitor [capacitance="100 nF" voltage=35V package="0603 [SMD, multilayer]"]
  R3 = Resistor [tolerance=±5% power=0.25W resistance=4.7k package=THT]

nets:
  VDD: U2.VDD, S1.Pin_3, S1.Pin_4, U1.VCC, U3.VDD, C1.0, R3.Pin_1
  N1: U2.DOUT, U1.RXI
  N2: U2.DIN, U1.TXO
  N3: U2.RESET, U1.D9
  GND: U2.GND, R2.Pin_0, R1.Pin_0, U1.GND, U3.GND, C1.1
  N4: LED1.cathode, U1.D3
  N5: LED1.anode, R2.Pin_1
  N6: S1.Pin_1, S1.Pin_2, R1.Pin_1, U1.D4
  N7: U1.D5, U3.DATA, R3.Pin_0
  12V: U1.RAW

notes:
  RESET BUTTON
  STATUS LIGHT
  DHT22 Sensor
