# Fritzing sketch HumbleRemote (saved by Fritzing 1.0.1rc)
breadboards: 1

parts:
  U2 = XBEE-1 [package=xbee-1_lock]
  LED1 = LED - 5mm [color="Red (633nm)" current=0.030 package="5 mm [THT]"]
  S1 = Pushbutton [package="[THT]"]
  R2 = Resistor [tolerance=±5% power=0.25 resistance=330 package=THT]
  R1 = Resistor [tolerance=±5% power=0.25 resistance=10k package=THT]
  U1 = Arduino Pro Micro (Clone)
  U3_DC-DC1_3_3V = DC_DC_XL4016 [package=board_screw]
  U4 = TRANSISTOR_NPN_2 [package=to-92]
  R4 = Resistor [tolerance=±5% power=0.25W resistance=330 package=THT]
  LED2 = LED - 5mm [color="Blue (470nm)" current=0.030A package="5 mm [THT]"]
  R5 = Resistor [tolerance=±5% power=0.25W resistance=10k package=THT]
  C1 = Ceramic Capacitor [capacitance=0.47mF voltage=35V package="100 mil [THT, multilayer]"]
  R6 = 12mm Trimmer Potentiometer (Large) [maximum_resistance=10kΩ knob_status=50% power=0.5W package=THT]

nets:
  VDD: U2.VDD, S1.Pin_3, S1.Pin_4, U1.VCC, U3_DC-DC1_3_3V.OUT+, LED2.anode, R6.leg2
  N1: U2.DOUT, U1.RXI
  N2: U2.DIN, U1.TXO
  N3: U2.RESET, U1.D16
  12V/GND/REMOTE - VCC: U2.GND, R2.Pin_0, R1.Pin_0, U1.GND, U3_DC-DC1_3_3V.IN+, U3_DC-DC1_3_3V.OUT-, U4.E, C1.1, R6.leg1
  N4: LED1.cathode, U1.D3
  N5: LED1.anode, R2.Pin_1
  N6: S1.Pin_1, S1.Pin_2, R1.Pin_1, U1.D4
  REMOTE - BUTTON1: U1.D5
  REMOTE - BUTTON2: U1.D6
  REMOTE - BUTTON3: U1.D7
  REMOTE - BUTTON4: U1.D8
  REMOTE - BUTTON5: U1.D9
  N7: U1.A0, R6.wiper
  REMOTE - GND: U3_DC-DC1_3_3V.IN-, C1.0
  N8: U4.C, R4.Pin_1
  N9: U4.B, R5.Pin_1
  N10: R4.Pin_0, LED2.cathode
  REMOTE - DATA: R5.Pin_0

notes:
  RESET BUTTON
  STATUS LIGHT
  Humble Remote
