# Fritzing sketch ThermostatProxy (saved by Fritzing 1.0.1rc)
breadboards: 1

parts:
  U1_Arduino_Nano_Every = Arduino Nano Every
  U4_DC-DC = DC_DC_XL4016 [package=board_screw]
  J1_BOILER = Screw terminal - 2 pins [package=THT]
  V2 = DC Power [voltage=24]
  D7_4148 = Diode [package=diode-1n4148]
  D8_4148 = Diode [package=diode-1n4148]
  D5_4148 = Diode [package=diode-1n4148]
  D6_4148 = Diode [package=diode-1n4148]
  D2_4_7V = Zener Diode [part_number=1N4732A breakdown_voltage=4.7V package="300 mil [THT]"]
  D3_13V = Zener Diode [part_number=1N4732A breakdown_voltage=13V package="300 mil [THT]"]
  D4_4_3V = Zener Diode [part_number=1N4732A breakdown_voltage=4.3V package="300 mil [THT]"]
  R1 = Resistor [tolerance=±5% power=0.25W resistance=330 package=THT]
  R2 = Resistor [tolerance=±5% power=0.25W resistance=220 package=THT]
  R3 = Resistor [tolerance=±5% power=0.25W resistance=100 package=THT]
  Q1_BC858B = PNP-Transistor [package="TO92 [THT]"]
  Q2_BC858B = PNP-Transistor [package="TO92 [THT]"]
  Q3_BC858B = PNP-Transistor [package="TO92 [THT]"]
  Q5_BC858B = PNP-Transistor [package="TO92 [THT]"]
  U2_PC817B = Sharp PC817 [package=THT]
  U3_PC817B = Sharp PC817 [package=THT]
  R4 = Resistor [tolerance=±5% power=0.25W resistance=330 package=THT]
  R5 = Resistor [tolerance=±5% power=0.25W resistance=10k package=THT]
  J2_THERMOSTAT = Screw terminal - 2 pins [package=THT]
  R6 = Resistor [tolerance=±5% power=0.25W resistance=33k package=THT]
  R7 = Resistor [tolerance=±5% power=0.25W resistance=100 package=THT]
  R8 = Resistor [tolerance=±5% power=0.25W resistance=20k package=THT]
  R9 = Resistor [tolerance=±5% power=0.25W resistance=39 package=THT]
  R10 = Resistor [tolerance=±5% power=0.25W resistance=4.7k package=THT]
  R11 = Resistor [tolerance=±5% power=0.25W resistance=10k package=THT]
  R15 = Resistor [tolerance=±5% power=0.25W resistance=1k package=THT]
  Q6_BC848C = NPN-Transistor [package="TO92 [THT]"]
  Q4_BC848C = NPN-Transistor [package="TO92 [THT]"]
  U5 = XBEE-1 [package=xbee-1_lock]
  LED2 = LED - 5mm [color="Red (633nm)" current=0.030 package="5 mm [THT]"]
  S1 = Pushbutton [package="[THT]"]
  R16 = Resistor [tolerance=±5% power=0.25 resistance=330 package=THT]
  R17 = Resistor [tolerance=±5% power=0.25 resistance=10k package=THT]
  R18 = Resistor [tolerance=±5% power=0.25W resistance=220 package=THT]
  R19 = Resistor [tolerance=±5% power=0.25W resistance=470 package=THT]

nets:
  N1: U1_Arduino_Nano_Every.RX, R18.Pin_1
  N2: U1_Arduino_Nano_Every.TX, U5.DOUT
  N3: U1_Arduino_Nano_Every.D2, U5.RESET
  SLAVE IN: U1_Arduino_Nano_Every.D4, U3_PC817B.Pin_3, R5.Pin_0
  SLAVE OUT: U1_Arduino_Nano_Every.D5~, R4.Pin_1
  MASTER OUT: U1_Arduino_Nano_Every.D6~, R10.Pin_1
  MASTER IN: U1_Arduino_Nano_Every.D7, R15.Pin_0, Q6_BC848C.E
  N4: U1_Arduino_Nano_Every.D8, S1.Pin_1, R17.Pin_1
  N5: U1_Arduino_Nano_Every.D9~, LED2.anode
  N6: U1_Arduino_Nano_Every.D11/MOSI, U1_Arduino_Nano_Every.+5V, U3_PC817B.Pin_4, Q6_BC848C.C, Q4_BC848C.B, S1.Pin_3, S1.Pin_4
  N7: U1_Arduino_Nano_Every.VIN, U4_DC-DC.OUT+
  GND: U1_Arduino_Nano_Every.GND, U1_Arduino_Nano_Every.D13~, U4_DC-DC.OUT-, U2_PC817B.Pin_2, R5.Pin_1, J2_THERMOSTAT.pin2, R6.Pin_0, R11.Pin_1, R15.Pin_1, U5.GND, R16.Pin_0, R17.Pin_0, R19.Pin_1
  3V3: U1_Arduino_Nano_Every.3V3, U5.VDD
  N8: U4_DC-DC.IN+, V2.V+, Q1_BC858B.E, Q3_BC858B.E, R7.Pin_1
  N9: U4_DC-DC.IN-, V2.V-
  N10: J1_BOILER.pin1, D8_4148.A, D5_4148.C
  N11: J1_BOILER.pin2, D7_4148.A, D6_4148.C
  N12: D7_4148.C, D8_4148.C, R1.Pin_0, Q5_BC858B.E
  N13: D5_4148.A, D6_4148.A, D2_4_7V.anode, D3_13V.anode, D4_4_3V.anode, R3.Pin_0, U3_PC817B.Pin_2
  N14: D2_4_7V.cathode, R2.Pin_1, Q5_BC858B.C
  N15: D3_13V.cathode, R1.Pin_1, Q5_BC858B.B, U2_PC817B.Pin_4
  N16: D4_4_3V.cathode, U2_PC817B.Pin_3
  N17: R2.Pin_0, R3.Pin_1, U3_PC817B.Pin_1
  N18: Q1_BC858B.B, Q2_BC858B.E, R7.Pin_0, R9.Pin_0
  N19: Q1_BC858B.C, Q2_BC858B.B, R6.Pin_1
  N20: Q2_BC858B.C, J2_THERMOSTAT.pin1, R8.Pin_0
  N21: Q3_BC858B.B, Q4_BC848C.C
  N22: Q3_BC858B.C, R9.Pin_1
  N23: U2_PC817B.Pin_1, R4.Pin_0
  N24: R8.Pin_1, R11.Pin_0, Q6_BC848C.B
  N25: R10.Pin_0, Q4_BC848C.E
  N26: U5.DIN, R18.Pin_0, R19.Pin_0
  N27: LED2.cathode, R16.Pin_1

notes:
  MASTER INTERFACE (BOILER)
  SLAVE INTERFACE (THERMOSTAT)
  STATUS LIGHT
  RESET BUTTON

custom parts:
  Arduino Nano Every: The Nano Every is Arduino’s 5V compatible board in the smallest available form factor: 45x18mm! The Arduino Nano is the preferred board for many projects requiring a small and easy to use microcontroller board. The small footprint and low price, make the Nano Every particularly suited for wearable inventions, low cost robotics, electronic musical instruments, and general use to control smaller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
